# Fritzing sketch wip (saved by Fritzing 0.9.6b)
breadboards: 1

parts:
  J1 = STM32 Nucleo boards
  LCD1 = LCD screen
  DHT = DHT22 module
  Relay = RELAY [package=relay-jzc]
  Light_Bulb = LEDs [package=led10mm]
  Wall_Plug = Lilypad Battery Connect
  PIR1 = PIR sensor

nets:
  N1: J1.D8, LCD1.RS
  N2: J1.D9_PWM, LCD1.E
  N3: J1.D10_PWM/SS, LCD1.DB4
  N4: J1.D11_PWM/MOSI, LCD1.DB5
  N5: J1.D12/MISO, LCD1.DB6
  N6: J1.D13/SCK, LCD1.DB7
  N7: J1.D2, PIR1.SIG
  N8: J1.D3_PWM, DHT.GND
  N9: J1.D4, Relay.COIL2
  VDD: J1.5V, LCD1.VDD, LCD1.LED+, DHT.VCC, Relay.NC, PIR1.VDD
  GND: J1.GND, LCD1.VSS, LCD1.V0, LCD1.R/W, LCD1.LED-, DHT.DATA, Relay.NO, PIR1.GND
  N10: Relay.MAIN, Light_Bulb.A
  N11: Relay.COIL1, Wall_Plug.+
  N12: Light_Bulb.C, Wall_Plug.-

custom parts:
  LEDs: LEDs Standard schematic elements and footprints for 5mm, 3mm, 1206, and 0603 sized LEDs. 5mm - Spark Fun Electronics SKU : COM-00529 (and others)
